// Logisim project PRESENT.circ as structural Verilog: 1 circuit, main circuit main
module main (
  input  [15:0] in_1,
  input  [31:0] in_2,
  input  [31:0] in_3,
  input  [31:0] in_4,
  input  [31:0] in_5,
  input  in_6,
  input  [4:0] in_7,
  input  [4:0] in_8,
  input  in_9,
  input  in_10,
  input  in_11,
  input  in_12,
  output [31:0] out_13,
  output [31:0] out_14,
  output [4:0] out_15,
  output [31:0] out_16
);

  wire and_2_out, clock_1_out, clock_2_out, not_1_out, not_3_out, or_2_out, undriven, undriven_2;
  wire [2:0] counter_1_q;
  wire [4:0] and_1_out, not_2_out, or_1_out;
  wire [15:0] main_4_out_6, multiplexer_3_out, register_5_q;
  wire [31:0] buffer_1_out, counter_2_q, main_1_p2, main_1_p4, main_2_out_4, main_2_out_5, main_3_out_4,
       main_3_out_5, main_4_out_5, main_4_out_7, multiplexer_1_out, multiplexer_2_out, multiplexer_4_out,
       multiplexer_5_out, register_1_q, register_2_q, register_3_q, register_4_q, xor_1_out, xor_3_out;

  Register #(.width(32)) register_1 (.D(out_13), .en(not_3_out), .Q(register_1_q), .clk(clock_2_out));  // open: clr
  assign xor_1_out = in_2 ^ main_2_out_4;  // XOR_Gate xor_1, 32 bits wide
  Multiplexer #(.width(32)) multiplexer_1 (
    .in0(xor_1_out), .in1(register_1_q), .out(multiplexer_1_out), .sel(or_2_out));  // open: en
  assign out_13 = main_1_p2 ^ main_3_out_4;  // XOR_Gate xor_2, 32 bits wide
  assign xor_3_out = in_3 ^ main_2_out_5;  // XOR_Gate xor_3, 32 bits wide
  Multiplexer #(.width(32)) multiplexer_2 (
    .in0(xor_3_out), .in1(register_2_q), .out(multiplexer_2_out), .sel(or_2_out));  // open: en
  // SPNet_main main_1: pin names not known; wires that end beside it: multiplexer_1_out, main_1_p2, multiplexer_2_out, main_1_p4
  Counter #(.width(3), .max('h7)) counter_1 (
    .count(in_9), .Q(counter_1_q), .clk(clock_1_out));  // open: load, D, carry, clr
  Counter #(.width(32), .max('hffffffff)) counter_2 (
    .load(in_9), .count(in_10), .Q(counter_2_q), .clk(clock_1_out));  // open: D, carry, clr
  assign out_14 = main_1_p4 ^ main_3_out_5;  // XOR_Gate xor_4, 32 bits wide
  SelectKey_main main_2 (.in_3(in_1), .in_1(in_4), .in_2(in_5), .out_4(main_2_out_4), .out_5(main_2_out_5));
  SelectKey_main main_3 (
    .in_3(main_4_out_6), .in_1(main_4_out_5), .in_2(main_4_out_7), .out_4(main_3_out_4), .out_5(main_3_out_5));
  Register #(.width(32)) register_2 (.D(out_14), .en(not_3_out), .Q(register_2_q), .clk(clock_2_out));  // open: clr
  assign buffer_1_out = counter_2_q;  // Buffer buffer_1, 32 bits wide
  Clock clock_1 (.out(clock_1_out));
  Multiplexer #(.width(16)) multiplexer_3 (
    .in0(in_1), .in1(register_5_q), .out(multiplexer_3_out), .sel(or_2_out), .en(undriven));
  Counter #(.width(5), .max('h1f)) counter_3 (
    .load(in_6), .count(not_3_out), .Q(out_15), .clk(clock_2_out));  // open: D, carry, clr
  Clock clock_2 (.out(clock_2_out));
  assign or_1_out = out_15 | in_7;  // OR_Gate or_1, 5 bits wide
  or or_2 (or_2_out, or_1_out[4], or_1_out[3], or_1_out[2], or_1_out[1], or_1_out[0]);
  RAM #(.addrWidth(3), .dataWidth(32), .bus("separate")) ram_1 (
    .addr(counter_1_q), .din(buffer_1_out), .data(out_16), .str(clock_1_out), .sel(in_11), .clk(clock_1_out),
    .ld(not_1_out), .clr(in_12));
  not not_1 (not_1_out, clock_1_out);
  Multiplexer #(.width(32)) multiplexer_4 (
    .in0(in_4), .in1(register_4_q), .out(multiplexer_4_out), .sel(or_2_out));  // open: en
  KeyT_main main_4 (
    .in_1(multiplexer_3_out), .in_2(multiplexer_4_out), .in_3(multiplexer_5_out), .out_6(main_4_out_6),
    .out_5(main_4_out_5), .out_7(main_4_out_7), .counter(out_15));
  Multiplexer #(.width(32)) multiplexer_5 (
    .in0(in_5), .in1(register_3_q), .out(multiplexer_5_out), .sel(or_2_out), .en(undriven_2));
  Register #(.width(32)) register_3 (
    .D(main_4_out_7), .en(not_3_out), .Q(register_3_q), .clk(clock_2_out));  // open: clr
  assign not_2_out = ~in_8;  // NOT_Gate not_2, 5 bits wide
  assign and_1_out = out_15 & not_2_out;  // AND_Gate and_1, 5 bits wide
  Register #(.width(32)) register_4 (
    .D(main_4_out_5), .en(not_3_out), .Q(register_4_q), .clk(clock_2_out));  // open: clr
  and and_2 (and_2_out, and_1_out[4], and_1_out[3], and_1_out[2], and_1_out[1], and_1_out[0]);
  not not_3 (not_3_out, and_2_out);
  Register #(.width(16)) register_5 (
    .D(main_4_out_6), .en(not_3_out), .Q(register_5_q), .clk(clock_2_out));  // open: clr

  // Notes on the sheet:
  //   out_16: pull=down
  //   add Round Key
  //   add Round Key
  //   sp layer
  //   select Key
  //   select Key
  //   ticks enable
  //   when str and sel is 1 then value at west edge is transferred to the RAM
  //   when ld and sel is 1 then value from selected address goes into east side D
  //   key transform
  //   select line control signal
endmodule
